// Logisim project Adder and Sub.circ as structural Verilog: 1 circuit, main circuit main
module main (
  input  A,
  input  B,
  input  A_2,
  input  B_2,
  input  A_3,
  input  B_3,
  input  C_in,
  input  C_in_2,
  input  C_in_3,
  input  A_4,
  input  B_4,
  input  A_5,
  input  B_5,
  input  A_6,
  input  B_6,
  input  C_in_4,
  input  A_7,
  input  B_7,
  input  B_8,
  input  A_8,
  input  A_9,
  input  B_9,
  input  C_in_5,
  output out_24,
  output out_25,
  output out_26,
  output out_27,
  output out_28,
  output out_29,
  output out_30,
  output out_31,
  output out_32
);

  wire and_1_out, and_2_out, and_3_out, and_4_out, and_5_out, and_6_out, and_7_out, and_8_out, and_9_out,
       and_10_out, and_11_out, and_12_out, and_13_out, and_14_out, and_15_out, and_16_out, and_17_out,
       and_18_out, not_1_out, not_2_out, not_3_out, not_4_out, not_5_out, not_6_out, not_7_out, not_8_out,
       not_9_out, not_10_out, not_11_out, not_12_out, not_13_out, or_1_out, or_2_out, or_3_out, or_4_out,
       or_5_out, or_6_out, or_7_out, or_8_out, or_9_out, xor_1_out, xor_2_out, xor_3_out, xor_7_out,
       xor_8_out, xor_9_out, xor_13_out, xor_14_out, xor_15_out;

  not not_1 (not_1_out, A_4);
  not not_2 (not_2_out, B_8);
  xor xor_1 (xor_1_out, A, B_2);
  and and_1 (and_1_out, A, B_2);
  xor xor_2 (xor_2_out, A_4, B_5);
  and and_2 (and_2_out, not_1_out, B_5);
  xor xor_3 (xor_3_out, A_7, B_8);
  and and_3 (and_3_out, A_7, not_2_out);
  not not_3 (not_3_out, xor_2_out);
  not not_4 (not_4_out, C_in_5);
  xor xor_4 (out_24, xor_1_out, C_in);
  and and_4 (and_4_out, C_in, xor_1_out);
  xor xor_5 (out_27, xor_2_out, C_in_4);
  and and_5 (and_5_out, not_3_out, C_in_4);
  xor xor_6 (out_30, xor_3_out, C_in_5);
  and and_6 (and_6_out, not_4_out, xor_3_out);
  or or_1 (or_1_out, and_4_out, and_1_out);
  or or_2 (or_2_out, and_5_out, and_2_out);
  or or_3 (or_3_out, and_6_out, and_3_out);
  // Probe on or_1_out
  // Probe on or_2_out
  // Probe on or_3_out
  not not_5 (not_5_out, A_3);
  not not_6 (not_6_out, A_6);
  not not_7 (not_7_out, A_9);
  xor xor_7 (xor_7_out, B, not_5_out);
  and and_7 (and_7_out, B, not_5_out);
  xor xor_8 (xor_8_out, B_4, not_6_out);
  and and_8 (and_8_out, B_4, not_6_out);
  xor xor_9 (xor_9_out, B_7, not_7_out);
  and and_9 (and_9_out, B_7, not_7_out);
  and and_10 (and_10_out, C_in_2, xor_7_out);
  xor xor_10 (out_25, xor_7_out, C_in_2);
  xor xor_11 (out_28, xor_8_out, or_4_out);
  and and_11 (and_11_out, or_4_out, xor_8_out);
  xor xor_12 (out_31, xor_9_out, or_5_out);
  and and_12 (and_12_out, or_5_out, xor_9_out);
  or or_4 (or_4_out, and_10_out, and_7_out);
  or or_5 (or_5_out, and_11_out, and_8_out);
  or or_6 (or_6_out, and_12_out, and_9_out);
  // Probe on or_4_out
  // Probe on or_5_out
  // Probe on or_6_out
  not not_8 (not_8_out, A_2);
  not not_9 (not_9_out, A_5);
  not not_10 (not_10_out, A_8);
  xor xor_13 (xor_13_out, A_2, B_3);
  and and_13 (and_13_out, not_8_out, B_3);
  xor xor_14 (xor_14_out, A_5, B_6);
  and and_14 (and_14_out, not_9_out, B_6);
  xor xor_15 (xor_15_out, A_8, B_9);
  and and_15 (and_15_out, not_10_out, B_9);
  not not_11 (not_11_out, xor_13_out);
  and and_16 (and_16_out, not_11_out, C_in_3);
  not not_12 (not_12_out, xor_14_out);
  not not_13 (not_13_out, xor_15_out);
  xor xor_16 (out_26, xor_13_out, C_in_3);
  xor xor_17 (out_29, xor_14_out, or_7_out);
  and and_17 (and_17_out, not_12_out, or_7_out);
  xor xor_18 (out_32, xor_15_out, or_8_out);
  and and_18 (and_18_out, not_13_out, or_8_out);
  or or_7 (or_7_out, and_16_out, and_13_out);
  or or_8 (or_8_out, and_17_out, and_14_out);
  or or_9 (or_9_out, and_18_out, and_15_out);
  // Probe on or_7_out
  // Probe on or_8_out
  // Probe on or_9_out
endmodule
