// Logisim project Half_adder.circ as structural Verilog: 1 circuit, main circuit main
module main (
);

  wire and_1_out, nor_1_out, nor_2_out, nor_3_out, nor_4_out, nor_5_out;

  and and_1 (and_1_out, 1'b1, 1'b1);
  nor nor_1 (nor_1_out, 1'b1, 1'b1);
  nor nor_2 (nor_2_out, 1'b1, 1'b1);
  nor nor_3 (nor_3_out, 1'b1, 1'b1);
  // Probe on and_1_out
  nor nor_4 (nor_4_out, nor_1_out, nor_2_out);
  nor nor_5 (nor_5_out, nor_4_out, nor_3_out);
  // Probe on nor_5_out
endmodule
