// Logisim project NOR gate.circ as structural Verilog: 1 circuit, main circuit main
module main (
);

  wire transistor_1_out, transistor_2_out;

  Transistor #(.\type ("n")) transistor_1 (.in(1'b0), .out(transistor_1_out), .gate(1'b0));
  Transistor transistor_2 (.in(1'b1), .out(transistor_2_out), .gate(1'b0));
  Transistor transistor_3 (.in(transistor_2_out), .out(transistor_1_out), .gate(1'b0));
  Transistor #(.\type ("n")) transistor_4 (.in(1'b0), .out(transistor_1_out), .gate(1'b0));
  // Probe on transistor_1_out
endmodule
