// Logisim project Posative-flip-flop-1.circ as structural Verilog: 1 circuit, main circuit main
module main (
  input  in_1
);

  wire _1_out, _2_out, _3_out, _4_out, _5_out, _6_out, _7_out, _8_out, _9_out, clock_1_out, nand_1_out;

  Clock clock_1 (.out(clock_1_out));
  nand nand_1 (nand_1_out, clock_1_out, clock_1_out);
  nand _1 (_1_out, in_1, nand_1_out);
  nand _2 (_2_out, _1_out, nand_1_out);
  nand _3 (_3_out, _1_out, _4_out);
  nand _4 (_4_out, _2_out, _3_out);
  nand _9 (_9_out, nand_1_out, nand_1_out);
  nand _5 (_5_out, _3_out, _9_out);
  nand _7 (_7_out, _5_out, _9_out);
  nand _6 (_6_out, _5_out, _8_out);
  nand _8 (_8_out, _7_out, _6_out);
  // Probe on _6_out
  // Probe on _8_out
endmodule
