// Logisim project Positive-flip-flop.circ as structural Verilog: 1 circuit, main circuit main
module main (
  input  in_1,
  output out_2,
  output out_3
);

  wire clock_1_out, nand_1_out, nand_2_out, nand_3_out, nand_4_out;

  Clock clock_1 (.out(clock_1_out));
  nand nand_1 (nand_1_out, nand_4_out, nand_2_out);
  nand nand_2 (nand_2_out, nand_1_out, clock_1_out);
  nand nand_3 (nand_3_out, nand_2_out, clock_1_out, nand_4_out);
  nand nand_4 (nand_4_out, nand_3_out, in_1);
  nand nand_5 (out_2, nand_2_out, out_3);
  nand nand_6 (out_3, out_2, nand_3_out);
endmodule
