// Logisim project SR Latch.circ as structural Verilog: 1 circuit, main circuit main
module main (
  input  in_1,
  input  in_2,
  input  in_3,
  input  in_4
);

  wire nand_1_out, nand_2_out, nor_1_out, nor_2_out;

  nand nand_1 (nand_1_out, in_1, nand_2_out);
  nand nand_2 (nand_2_out, nand_1_out, in_2);
  nor nor_1 (nor_1_out, in_3, nor_2_out);
  nor nor_2 (nor_2_out, nor_1_out, in_4);
  // Probe on nand_1_out
  // Probe on nand_2_out
  // Probe on nor_1_out
  // Probe on nor_2_out
endmodule
