// Logisim project Shift-register.circ as structural Verilog: 1 circuit, main circuit main
module main (
  input  in_1
);

  wire _1_2_out, _1_out, _2_2_out, _2_out, _3_2_out, _3_out, _4_2_out, _4_out, _5_2_out, _5_out, _6_2_out,
       _6_out, _7_2_out, _7_out, _8_2_out, _8_out, _9_2_out, _9_out, and_1_out, clock_1_out;

  Clock clock_1 (.out(clock_1_out));
  and and_1 (and_1_out, clock_1_out, clock_1_out);
  nand _1 (_1_out, in_1, and_1_out);
  nand _2 (_2_out, _1_out, and_1_out);
  nand _3 (_3_out, _1_out, _4_out);
  nand _4 (_4_out, _2_out, _3_out);
  nand _9 (_9_out, and_1_out, and_1_out);
  nand _5 (_5_out, _3_out, _9_out);
  nand _7 (_7_out, _5_out, _9_out);
  nand _6 (_6_out, _5_out, _8_out);
  nand _8 (_8_out, _7_out, _6_out);
  // Probe on _6_out
  // Probe on _8_out
  nand _1_2 (_1_2_out, _6_out, and_1_out);
  nand _2_2 (_2_2_out, _1_2_out, and_1_out);
  nand _3_2 (_3_2_out, _1_2_out, _4_2_out);
  nand _4_2 (_4_2_out, _2_2_out, _3_2_out);
  nand _9_2 (_9_2_out, and_1_out, and_1_out);
  nand _5_2 (_5_2_out, _3_2_out, _9_2_out);
  nand _7_2 (_7_2_out, _5_2_out, _9_2_out);
  nand _6_2 (_6_2_out, _5_2_out, _8_2_out);
  nand _8_2 (_8_2_out, _7_2_out, _6_2_out);
  // Probe on _6_2_out
  // Probe on _8_2_out
endmodule
