// Logisim project difference of full subtractir.circ as structural Verilog: 1 circuit, main circuit main
module main (
  input  B,
  input  A,
  input  A_2,
  input  B_2,
  input  C_in,
  input  C_in_2,
  input  B_3,
  input  A_3,
  input  A_4,
  input  B_4,
  input  B_5,
  input  A_5,
  input  A_6,
  input  B_6,
  output out_15,
  output out_16,
  output out_17,
  output out_18,
  output out_19,
  output out_20
);

  wire and_1_out, and_2_out, and_3_out, and_4_out, and_5_out, and_6_out, and_7_out, and_8_out, and_9_out,
       and_10_out, and_11_out, and_12_out, not_1_out, not_2_out, not_3_out, not_4_out, not_5_out, not_6_out,
       not_7_out, not_8_out, not_9_out, or_1_out, or_2_out, or_3_out, or_4_out, or_5_out, or_6_out,
       xor_1_out, xor_2_out, xor_3_out, xor_7_out, xor_8_out, xor_9_out;

  not not_1 (not_1_out, A_2);
  not not_2 (not_2_out, A_4);
  not not_3 (not_3_out, A_6);
  xor xor_1 (xor_1_out, B, not_1_out);
  and and_1 (and_1_out, B, not_1_out);
  xor xor_2 (xor_2_out, B_3, not_2_out);
  and and_2 (and_2_out, B_3, not_2_out);
  xor xor_3 (xor_3_out, B_5, not_3_out);
  and and_3 (and_3_out, B_5, not_3_out);
  xor xor_4 (out_15, xor_1_out, C_in);
  and and_4 (and_4_out, C_in, xor_1_out);
  xor xor_5 (out_17, xor_2_out, or_1_out);
  and and_5 (and_5_out, or_1_out, xor_2_out);
  xor xor_6 (out_19, xor_3_out, or_2_out);
  and and_6 (and_6_out, or_2_out, xor_3_out);
  or or_1 (or_1_out, and_4_out, and_1_out);
  or or_2 (or_2_out, and_5_out, and_2_out);
  or or_3 (or_3_out, and_6_out, and_3_out);
  // Probe on or_1_out
  // Probe on or_2_out
  // Probe on or_3_out
  not not_4 (not_4_out, A);
  xor xor_7 (xor_7_out, A, B_2);
  and and_7 (and_7_out, not_4_out, B_2);
  not not_5 (not_5_out, A_3);
  not not_6 (not_6_out, A_5);
  not not_7 (not_7_out, xor_7_out);
  xor xor_8 (xor_8_out, A_3, B_4);
  and and_8 (and_8_out, not_5_out, B_4);
  xor xor_9 (xor_9_out, A_5, B_6);
  and and_9 (and_9_out, not_6_out, B_6);
  and and_10 (and_10_out, not_7_out, C_in_2);
  not not_8 (not_8_out, xor_8_out);
  not not_9 (not_9_out, xor_9_out);
  xor xor_10 (out_16, xor_7_out, C_in_2);
  xor xor_11 (out_18, xor_8_out, or_4_out);
  and and_11 (and_11_out, not_8_out, or_4_out);
  xor xor_12 (out_20, xor_9_out, or_5_out);
  and and_12 (and_12_out, not_9_out, or_5_out);
  or or_4 (or_4_out, and_10_out, and_7_out);
  or or_5 (or_5_out, and_11_out, and_8_out);
  or or_6 (or_6_out, and_12_out, and_9_out);
  // Probe on or_4_out
  // Probe on or_5_out
  // Probe on or_6_out
endmodule
