// Logisim project jk-ff-complete.circ as structural Verilog: 1 circuit, main circuit main
module main (
  input  Reset_prime,
  input  J,
  input  K,
  input  Reset_prime_2,
  input  J_2,
  input  in_6,
  output out_7,
  output out_8
);

  wire _3_out, _4_out, _5_out, _6_out, _7_out, _8_out, _9_out, clock_1_out, clock_2_out, multiplexer_1_out,
       multiplexer_2_out, multiplexer_3_out, multiplexer_4_out, multiplexer_5_out, multiplexer_6_out,
       multiplexer_7_out, multiplexer_8_out, nand_1_out, nand_2_out, nand_3_out, nand_4_out;

  Clock clock_1 (.out(clock_1_out));
  Clock clock_2 (.out(clock_2_out));
  Multiplexer multiplexer_1 (.in0(_8_out), .in1(1'b0), .out(multiplexer_1_out), .sel(Reset_prime));  // open: en
  Multiplexer multiplexer_2 (.in0(J), .in1(1'b0), .out(multiplexer_2_out), .sel(Reset_prime));  // open: en
  Multiplexer multiplexer_3 (.in0(K), .in1(1'b1), .out(multiplexer_3_out), .sel(Reset_prime));  // open: en
  Multiplexer multiplexer_4 (.in0(_6_out), .in1(1'b1), .out(multiplexer_4_out), .sel(Reset_prime));  // open: en
  Multiplexer multiplexer_5 (.in0(out_8), .in1(1'b0), .out(multiplexer_5_out), .sel(Reset_prime_2));  // open: en
  Multiplexer multiplexer_6 (.in0(J_2), .in1(1'b0), .out(multiplexer_6_out), .sel(Reset_prime_2));  // open: en
  Multiplexer multiplexer_7 (.in0(in_6), .in1(1'b1), .out(multiplexer_7_out), .sel(Reset_prime_2));  // open: en
  Multiplexer multiplexer_8 (.in0(out_7), .in1(1'b1), .out(multiplexer_8_out), .sel(Reset_prime_2));  // open: en
  nand nand_1 (nand_1_out, multiplexer_1_out, clock_1_out, multiplexer_2_out);
  nand nand_2 (nand_2_out, multiplexer_3_out, clock_1_out, multiplexer_4_out);
  nand nand_3 (nand_3_out, multiplexer_5_out, clock_2_out, multiplexer_6_out);
  nand nand_4 (nand_4_out, multiplexer_7_out, clock_2_out, multiplexer_8_out);
  nand _3 (_3_out, nand_1_out, _4_out);
  nand _4 (_4_out, nand_2_out, _3_out);
  nand nand_5 (out_7, nand_3_out, out_8);
  nand nand_6 (out_8, out_7, nand_4_out);
  nand _9 (_9_out, clock_1_out, clock_1_out);
  nand _5 (_5_out, _3_out, _9_out);
  nand _7 (_7_out, _4_out, _9_out);
  nand _6 (_6_out, _5_out, _8_out);
  nand _8 (_8_out, _7_out, _6_out);
  // Probe on _6_out
  // Probe on _8_out

  // Notes on the sheet:
  //   Clock
  //   Feedback X
  //   Feedback Y
  //   Feedback X
  //   Feedback Y
endmodule
